# Fritzing sketch schematic (saved by Fritzing 0.9.5d)
breadboards: 1

parts:
  Деталь1 = Arduino Nano (Rev3.0)
  S1 = Pushbutton [package="[THT]"]
  S2 = Pushbutton [package="[THT]"]
  S3 = Pushbutton [package="[THT]"]
  S4 = Pushbutton [package="[THT]"]
  Encoder_round1 = Encoder round
  U1 = WS2812 RGB LED strip
  VCC1 = 4 x AAA Battery Mount
  Деталь2 = LCD1602-I2C

nets:
  GND: Деталь1.GND, S1.Pin_1, S1.Pin_2, S2.Pin_1, S2.Pin_2, S3.Pin_1, S3.Pin_2, S4.Pin_1, S4.Pin_2, Encoder_round1.pin1, U1.GND, VCC1.-, Деталь2.GND
  N1: Деталь1.D2, S1.Pin_3
  N2: Деталь1.D3, S2.Pin_3, S2.Pin_4
  N3: Деталь1.D4, S3.Pin_3, S3.Pin_4
  N4: Деталь1.D5, S4.Pin_3, S4.Pin_4
  N5: Деталь1.D6, Encoder_round1.pin4
  N6: Деталь1.D7, Encoder_round1.pin3
  N7: Деталь1.D8, Encoder_round1.pin2
  N8: Деталь1.D9, U1.DIN
  VCC: Деталь1.5V, Encoder_round1.pin5, U1.VCC, VCC1.+, Деталь2.VCC
  N9: Деталь1.A5, Деталь2.SCL
  N10: Деталь1.A4, Деталь2.SDA

custom parts:
  WS2812 RGB LED strip: WS2812 strip
  4 x AAA Battery Mount: A 4 x AAA battery pack (4.8 Volts with recharables)
  LCD1602-I2C: A standard character display, usually with 2x16 characters. Comes in many colors with LCM1602 IIC attached.
